# Fritzing sketch diagram (saved by Fritzing 0.9.3b)
breadboards: 1

parts:
  Raspberry_Pi_1 = Raspberry Pi 3 [part_number=RPI-3-V1.2]
  S1 = Round Pushbutton
  S2 = Round Pushbutton
  LED1 = LED - 5mm [color="Red (633nm)" package="5 mm [THT]"]
  R1 = Resistor [tolerance=±5% resistance=330 package="2010 [SMD]"]

nets:
  N1: Raspberry_Pi_1.GIPO26, S2.leg1
  N2: Raspberry_Pi_1.GND, S1.leg0, S2.leg0, LED1.cathode
  N3: Raspberry_Pi_1.GIPO16, S1.leg1
  N4: Raspberry_Pi_1.GIPO12, R1.Pin_1
  N5: LED1.anode, R1.Pin_0
